# Fritzing sketch Clave_acceso (saved by Fritzing 0.9.3b)
breadboards: 1

parts:
  Componente2 = Arduino Uno (Rev3)
  U1 = LCD-16X2 [package=lcd-16x2]
  LCM1602_IIC1 = LCM1602 IIC [part_number="LCM1602 IIC" chip_label="LCM1602 IIC" package="DIP (Dual Inline) [THT]"]
  Keypad4x1 = Keypad Membran 4x4

nets:
  N1: Componente2.A4/SDA, LCM1602_IIC1.SDA
  N2: Componente2.A5/SCL, LCM1602_IIC1.SCL
  N3: Componente2.D8, Keypad4x1.Pin2
  N4: Componente2.D9_PWM, Keypad4x1.Pin1
  N5: Componente2.D2, Keypad4x1.Pin8
  N6: Componente2.D3_PWM, Keypad4x1.Pin7
  N7: Componente2.D4, Keypad4x1.Pin6
  N8: Componente2.D5_PWM, Keypad4x1.Pin5
  N9: Componente2.D6_PWM, Keypad4x1.Pin4
  N10: Componente2.D7, Keypad4x1.Pin3
  5V: Componente2.5V, LCM1602_IIC1.VCC
  GND: Componente2.GND, LCM1602_IIC1.GND
  VSS: U1.VSS, LCM1602_IIC1.VSS
  VDD: U1.VDD, LCM1602_IIC1.VDD
  N11: U1.VO, LCM1602_IIC1.V0
  N12: U1.RS, LCM1602_IIC1.RS
  N13: U1.R_W, LCM1602_IIC1.RW
  N14: U1.E, LCM1602_IIC1.E
  N15: U1.DB0, LCM1602_IIC1.D0
  N16: U1.DB1, LCM1602_IIC1.D1
  N17: U1.DB2, LCM1602_IIC1.D2
  N18: U1.DB3, LCM1602_IIC1.D3
  N19: U1.DB4, LCM1602_IIC1.D4
  N20: U1.DB5, LCM1602_IIC1.D5
  N21: U1.DB6, LCM1602_IIC1.D6
  N22: U1.DB7, LCM1602_IIC1.D7
  N23: U1.A, LCM1602_IIC1.A
  N24: U1.K, LCM1602_IIC1.K

custom parts:
  LCM1602 IIC: I2C-Module to use a 1602 or 2004 LCD on with the wire.h libory Serial LCD Modul
  Keypad Membran 4x4: Membrane Keypad 4x4 Matrix
