# Fritzing sketch Display7S1P (saved by Fritzing 0.9.3b)
breadboards: 1

parts:
  Componente1 = Arduino Uno (Rev3)
  7_Segment1 = 7-Segment LED Display [package=THT]
  R1 = Resistor [tolerance=±5% resistance=680 package=THT]

nets:
  N1: Componente1.D8, 7_Segment1.cathodeC
  N2: Componente1.D9_PWM, 7_Segment1.cathodeDP
  N3: Componente1.D10_PWM/SS, 7_Segment1.cathodeG
  N4: Componente1.D11_PWM/MOSI, 7_Segment1.cathodeF
  N5: Componente1.D12/MISO, 7_Segment1.cathodeA
  N6: Componente1.D13/SCK, 7_Segment1.cathodeB
  N7: Componente1.D6_PWM, 7_Segment1.cathodeE
  N8: Componente1.D7, 7_Segment1.cathodeD
  N9: Componente1.5V, R1.Pin_0
  N10: 7_Segment1.commAnode#7, R1.Pin_1
