# Fritzing sketch Joystick_LCD (saved by Fritzing 0.9.3b)
breadboards: 1

parts:
  Componente2 = Arduino Uno (Rev3)
  Componente3 = Black Joystick KY-023
  U1 = LCD-16X2 [package=lcd-16x2]
  LCM1602_IIC1 = LCM1602 IIC [part_number="LCM1602 IIC" chip_label="LCM1602 IIC" package="DIP (Dual Inline) [THT]"]

nets:
  N1: Componente2.A0, Componente3.VRx
  N2: Componente2.A1, Componente3.VRy
  N3: Componente2.A4/SDA, LCM1602_IIC1.SDA
  N4: Componente2.A5/SCL, LCM1602_IIC1.SCL
  N5: Componente2.D10_PWM/SS, Componente3.SW
  5V: Componente2.5V, Componente3.+5V, LCM1602_IIC1.VCC
  GND: Componente2.GND, Componente3.GND, LCM1602_IIC1.GND
  VSS: U1.VSS, LCM1602_IIC1.VSS
  VDD: U1.VDD, LCM1602_IIC1.VDD
  N6: U1.VO, LCM1602_IIC1.V0
  N7: U1.RS, LCM1602_IIC1.RS
  N8: U1.R_W, LCM1602_IIC1.RW
  N9: U1.E, LCM1602_IIC1.E
  N10: U1.DB0, LCM1602_IIC1.D0
  N11: U1.DB1, LCM1602_IIC1.D1
  N12: U1.DB2, LCM1602_IIC1.D2
  N13: U1.DB3, LCM1602_IIC1.D3
  N14: U1.DB4, LCM1602_IIC1.D4
  N15: U1.DB5, LCM1602_IIC1.D5
  N16: U1.DB6, LCM1602_IIC1.D6
  N17: U1.DB7, LCM1602_IIC1.D7
  N18: U1.A, LCM1602_IIC1.A
  N19: U1.K, LCM1602_IIC1.K

custom parts:
  Black Joystick KY-023: Description: The joystick is a combination of 2 analoog potentiometer and a digital switch. Arduino GND --> Module pin - Arduino +5V --> Module pin +5V Arduino Analoog 0 --> Module VRx Arduino Analoog 1 --> Module VRy Arduino Digital --> Module SW Dimensions: 1" x 1.25"
  LCM1602 IIC: I2C-Module to use a 1602 or 2004 LCD on with the wire.h libory Serial LCD Modul
