# Fritzing sketch Keypad4x4 (saved by Fritzing 0.9.3b)

parts:
  Componente1 = Arduino Uno (Rev3)
  Keypad4x1 = Keypad Membran 4x4

nets:
  N1: Componente1.D8, Keypad4x1.Pin2
  N2: Componente1.D9_PWM, Keypad4x1.Pin1
  N3: Componente1.D2, Keypad4x1.Pin8
  N4: Componente1.D3_PWM, Keypad4x1.Pin7
  N5: Componente1.D4, Keypad4x1.Pin6
  N6: Componente1.D5_PWM, Keypad4x1.Pin5
  N7: Componente1.D6_PWM, Keypad4x1.Pin4
  N8: Componente1.D7, Keypad4x1.Pin3

custom parts:
  Keypad Membran 4x4: Membrane Keypad 4x4 Matrix
