# Fritzing sketch LCD16x2 (saved by Fritzing 0.9.3b)
breadboards: 1

parts:
  LCD1 = LCD screen
  Componente1 = Arduino Uno (Rev3)
  R1 = Resistor [tolerance=±5% resistance=220 package=THT]
  R2 = Rotary Potentiometer (Large) [maximum_resistance=100kΩ package=THT]

nets:
  VSS: LCD1.VSS, LCD1.LED-, Componente1.GND
  VDD: LCD1.VDD, Componente1.5V, R1.Pin_0, R2.leg1, R2.leg2
  N1: LCD1.V0, R2.wiper
  N2: LCD1.RS, Componente1.D12/MISO
  N3: LCD1.R/W, Componente1.D11_PWM/MOSI
  N4: LCD1.DB4, Componente1.D5_PWM
  N5: LCD1.DB5, Componente1.D4
  N6: LCD1.DB6, Componente1.D3_PWM
  N7: LCD1.DB7, Componente1.D2
  N8: LCD1.LED+, R1.Pin_1
