# Fritzing sketch LED_Fotocelda (saved by Fritzing 0.9.4)
breadboards: 1

parts:
  R2 = Resistor [tolerance=±5% resistance=220 package=THT]
  R1 = Photocell (LDR) [package=THT]
  Componente1 = Arduino Uno (Rev3)
  R3 = Rotary Potentiometer (Large) [maximum_resistance=100kΩ package=THT]
  LED1 = LED - 5mm [color="Blue (430nm)" package="5 mm [THT]"]
  R4 = Resistor [tolerance=±20% resistance=220 package=THT]

nets:
  N1: R2.Pin_0, R1.pin_1, Componente1.A1
  N2: R2.Pin_1, Componente1.5V, R3.leg1
  N3: R1.pin_0, R3.leg2, R4.Pin_0
  N4: Componente1.A0, R3.wiper
  N5: Componente1.D13/SCK, LED1.anode
  N6: LED1.cathode, R4.Pin_1

// code stored in the sketch: LED_CON_FOTOCELDA.ino
//Totalmente creado por LPZ ELECTRONICS para: YouTube (www.youtube.com/antoniolr95), Taringa y http://antoniolr95.blogspot.com


#define LED 9     //El LED esta conectado en el pin 9 
#define LDR 0     //El LDR esta conectador en el pin A0

int luz = 0;       
int valor_sensor = 0;       
int valor_limite = 470;  //Este valor hara que el LED cambie de estado a una determinada luminosidad (podeis con distintos valores para ajustar la sensibilidad)


void setup() {      //Configuracion de los pin como entrada o salida 
  Serial.begin(9600);    
  pinMode(LED,OUTPUT);
  pinMode(LDR,INPUT);
}

void loop ()  //Configuracion de los valores del LDR
{
  valor_sensor = analogRead(LDR); 
  luz = (5.0 * valor_sensor * 100.0)/1024.0; //Para entender esta formula visitar: http://programarfacil.com/podcast/48-sensor-de-temperatura-en-arduino/
  Serial.print(luz);  
  Serial.println(" Luz");             
  delay(300);                       
  
  if (luz <= valor_limite)   //Si el valor de luz es menor o igual que el valor limite
  {
    digitalWrite (LED, LOW);  //El led se apaga
  }
  if (luz > valor_limite)   //Si es mayor que el valor limite
  {
    digitalWrite (LED, HIGH);  //El led se eniende
  }
}
