# Fritzing sketch LED_Pulsador (saved by Fritzing 0.9.3b)
breadboards: 1

parts:
  Componente1 = Arduino Uno (Rev3)
  LED1 = LED - 5mm [color="Green (570nm)" package="5 mm [THT]"]
  R1 = Resistor [tolerance=±5% resistance=220 package=THT]
  S1 = Pushbutton [package="[THT]"]
  R2 = Resistor [tolerance=±5% resistance=220 package=THT]

nets:
  N1: Componente1.D11_PWM/MOSI, S1.Pin_3, S1.Pin_4, R2.Pin_0
  N2: Componente1.D13/SCK, LED1.anode
  N3: Componente1.GND, S1.Pin_1, S1.Pin_2
  N4: Componente1.5V, R1.Pin_1, R2.Pin_1
  N5: LED1.cathode, R1.Pin_0
