# Fritzing sketch LED_RGB (saved by Fritzing 0.9.3b)
breadboards: 1

parts:
  Componente1 = Arduino Uno (Rev3)
  LED1 = RGB LED (com. cathode, rgb) [package="5 mm [THT]"]
  R1 = Resistor [tolerance=±5% resistance=220 package=THT]
  R2 = Resistor [tolerance=±5% resistance=220 package=THT]
  R3 = Resistor [tolerance=±5% resistance=220 package=THT]

nets:
  N1: Componente1.D3_PWM, R3.Pin_0
  N2: Componente1.D5_PWM, R2.Pin_0
  N3: Componente1.D6_PWM, R1.Pin_0
  N4: Componente1.GND, LED1.blue_anode
  N5: LED1.red_anode, R1.Pin_1
  N6: LED1.common_cathode, R2.Pin_1
  N7: LED1.green_anode, R3.Pin_1

// code stored in the sketch: LED_RGB.ino
int ledRojo =6;//se definen los pines donde irán las patas del led RGB con su respectivo color  
int ledVerde=5; 
int ledAzul=3;

void setup() {
pinMode(ledRojo,OUTPUT);//se definen los pines como salida
pinMode(ledVerde,OUTPUT);
pinMode(ledAzul,OUTPUT);
}

void loop() {
analogWrite(ledRojo,0);//se le asignan los valores al color rojo
analogWrite(ledVerde,255);//se le asignan los valores al color verde
analogWrite(ledAzul,255);//se le asignan los valores al color amarillo
delay(1000);
}
