# Fritzing sketch LED_Receptor_infrarrojo (saved by Fritzing 0.9.3b)
breadboards: 1

parts:
  IR1 = TSOP312.., 314.. [package=THT]
  Componente1 = Arduino Uno (Rev3)
  LED1 = LED - 5mm [color="Orange (620nm)" package="5 mm [THT]"]
  R1 = Resistor [tolerance=±5% resistance=220 package=THT]

nets:
  N1: IR1.GND, Componente1.D11_PWM/MOSI
  N2: IR1.Data, Componente1.5V, R1.Pin_1
  N3: Componente1.D13/SCK, LED1.anode
  N4: LED1.cathode, R1.Pin_0
