# Fritzing sketch LED_SW520D (saved by Fritzing 0.9.3b)
breadboards: 1

parts:
  Componente1 = Arduino Uno (Rev3)
  S1 = Tilt Switch [package=THT]
  R1 = Resistor [tolerance=±5% resistance=220 package=THT]
  LED1 = LED - 5mm [color="Red (633nm)" package="5 mm [THT]"]

nets:
  N1: Componente1.D13/SCK, LED1.anode
  N2: Componente1.GND, S1.Pin_2, LED1.cathode
  N3: Componente1.D2, S1.Pin_1, R1.Pin_0
  N4: Componente1.5V, R1.Pin_1

// code stored in the sketch: SENSOR_DE_INCLINACION.ino
int LED=13;//se define el pin donde irá el led
int SENSOR=2;//se define el pin donde irá el sensor

void setup(){
  Serial.begin(9600);
  pinMode(LED,OUTPUT);//se define el led como salida y el sensor como entrada
  pinMode(SENSOR, INPUT);
  digitalWrite(LED, LOW);//el led comienza apagado para evitar errores
}

void loop(){
digitalWrite(LED,LOW);
if(digitalRead(SENSOR)==1){
  Serial.println("Alerta por inclinacion");
  digitalWrite(LED,HIGH);
  delay(2000);
}
}
