# Fritzing sketch LED_Suiche (saved by Fritzing 0.9.3b)
breadboards: 1

parts:
  Componente1 = Arduino Uno (Rev3)
  LED1 = LED - 5mm [color="Orange (620nm)" package="5 mm [THT]"]
  R1 = Resistor [tolerance=±5% resistance=220 package=THT]
  R2 = Resistor [tolerance=±5% resistance=220 package=THT]
  S3 = Pushbutton [package=THT]

nets:
  N1: Componente1.D11_PWM/MOSI, S3.leg1
  N2: Componente1.D13/SCK, LED1.anode
  N3: Componente1.5V, R1.Pin_1, R2.Pin_1
  N4: LED1.cathode, R1.Pin_0
  N5: R2.Pin_0, S3.leg0
