# Fritzing sketch LED_WiFi (saved by Fritzing 0.9.3b)

parts:
  U1 = NodeMCU V1.0
  LED1 = LED - 5mm [color="Green (555nm)" package="5 mm [THT]"]

nets:
  N1: U1.D0, LED1.anode
  N2: U1.GND, LED1.cathode

custom parts:
  NodeMCU V1.0: ESP8266 based NodeMCU
