# Fritzing sketch Luces_WiFi (saved by Fritzing 0.9.3b)
breadboards: 1

parts:
  U1 = NodeMCU V1.0
  KY-1 = Keyes Relay [package=THT]
  KY-2 = Keyes Relay [package=THT]
  J1 = 220v plug
  J2 = 220v plug
  BULB2 = Incandescent light bulb small [package="bulb sm"]
  BULB1 = Incandescent light bulb small [package="bulb sm"]

nets:
  N1: U1.D0, KY-1.signal
  N2: U1.D1, KY-2.signal
  N3: U1.3V3, KY-1.power, KY-2.power
  N4: U1.GND, KY-1.ground, KY-2.ground
  N5: KY-1.C, J2.pin1
  N6: KY-1.NO, BULB1.2
  N7: KY-2.C, J1.pin1
  N8: KY-2.NO, BULB2.2
  N9: J1.pin2, BULB2.1
  N10: J2.pin2, BULB1.1

custom parts:
  NodeMCU V1.0: ESP8266 based NodeMCU
  Keyes Relay: The Keyes 5V relay module is suitable for SCM development, home appliance control. It uses a 5V~12V TIL control signal which can control DC / AC signal.
  220v plug: Generic 220V AC plug.
