# Fritzing sketch Matriz_LED_8x32 (saved by Fritzing 0.9.3b)

parts:
  M1 = MAX7219 8x8 single Led Matrix Module
  Componente1 = Arduino Uno (Rev3)

nets:
  N1: M1.I-CLK-1, M1.O-CLK-1, Componente1.5V
  N2: M1.I-CS-1, M1.O-CS-1, Componente1.GND
  N3: M1.I-DIN-1, Componente1.D11_PWM/MOSI
  N4: M1.I-GND-1, M1.O-GND-1, Componente1.D10_PWM/SS
  N5: M1.I-VCC-1, M1.O-VCC-1, Componente1.D13/SCK

custom parts:
  MAX7219 8x8 single Led Matrix Module: Description: MAX7219 8x8 LedMatrix single Red Module Dimensions: 32x32mm Documents:
