# Fritzing sketch Micro_servomotor (saved by Fritzing 0.9.3b)

parts:
  Componente1 = Arduino Uno (Rev3)
  M2 = Dagu DGServo 9g (Top view) [part_number=RS001B]

nets:
  N1: Componente1.D9_PWM, M2.pulse
  GND: Componente1.GND, M2.gnd
  5V: Componente1.5V, M2.vcc
