# Fritzing sketch OLED128x64 (saved by Fritzing 0.9.3b)
breadboards: 1

parts:
  OLED_I2C1 = OLED 128x64 I2C Monochrome Display
  Componente1 = Arduino Nano (Rev3.0) (ICSP)
  R1 = Resistor [tolerance=±5% resistance=10k package=THT]
  R2 = Resistor [tolerance=±5% resistance=10k package=THT]

nets:
  N1: OLED_I2C1.SDA, Componente1.A4, R2.Pin_1
  N2: OLED_I2C1.SCK, Componente1.A5, R1.Pin_1
  VDD: OLED_I2C1.VDD, Componente1.5V, R1.Pin_0, R2.Pin_0
  GND: OLED_I2C1.GND, Componente1.GND
