# Fritzing sketch Pulsador_interruptor (saved by Fritzing 0.9.3b)
circuit board: 8.46667cm x 5.64444cm
breadboards: 1

parts:
  Componente1 = Arduino Uno (Rev3)
  S1 = Pushbutton [package="[THT]"]
  LED1 = LED - 5mm [color="Red (633nm)" package="5 mm [THT]"]
  R1 = Resistor [tolerance=±10% resistance=220 package=THT]
  R2 = Resistor [tolerance=±5% resistance=220 package=THT]

nets (from the breadboard view):
  N1: Componente1.D2, S1.Pin_3, S1.Pin_4, R2.Pin_0
  N2: Componente1.D4, LED1.anode
  N3: Componente1.5V, R2.Pin_1
  N4: Componente1.GND, S1.Pin_1, S1.Pin_2, R1.Pin_1
  N5: LED1.cathode, R1.Pin_0

// code stored in the sketch: PULSADOR_A_INTERRUPTOR.ino
int PULSADOR= 2;//se nombran los pines donde irán el PULSADOR y el LED
int LED=4;
int estado=0;//definimos las variables para guardar el estado del PULSADOR y el LED
int estadoLED=0;

void setup (){
pinMode(PULSADOR,INPUT);//definimos como pin de entrada al PULSADOR
pinMode(LED,OUTPUT);//definimos como pin de salida al LED
digitalWrite(LED,LOW);//iniciamos con el LED apagado para evitar errores
}

void loop(){
estado=digitalRead(PULSADOR);//definimos como "estado" a la lectura del PULSADOR
if (estado==LOW){//iniciamos un ciclo para cuando se oprima el pulsador
  estadoLED=digitalRead(4);//definimos como "estadoLED" la lectura del LED
  digitalWrite(LED,!estadoLED);//cambiamos el estado del LED
  delay(1000);//damos una espera de un segundo para evitar errores
}
}
