# Fritzing sketch Semaforo (saved by Fritzing 0.9.3b)
breadboards: 1

parts:
  Componente1 = Arduino Uno (Rev3)
  LED1 = LED - 5mm [color="Red (633nm)" package="5 mm [THT]"]
  LED2 = LED - 5mm [color="Yellow (585nm)" package="5 mm [THT]"]
  LED3 = LED - 5mm [color="Green (555nm)" package="5 mm [THT]"]
  R1 = Resistor [tolerance=±5% resistance=330 package=THT]
  R2 = Resistor [tolerance=±5% resistance=330 package=THT]
  R3 = Resistor [tolerance=±5% resistance=330 package=THT]

nets:
  N1: Componente1.D10_PWM/SS, LED1.anode
  N2: Componente1.D11_PWM/MOSI, LED2.anode
  N3: Componente1.D12/MISO, LED3.anode
  N4: Componente1.GND, R1.Pin_1, R2.Pin_1, R3.Pin_1
  N5: LED1.cathode, R2.Pin_0
  N6: LED2.cathode, R1.Pin_0
  N7: LED3.cathode, R3.Pin_0

// code stored in the sketch: SEMAFORO.ino
int LED_ROJO=A0;//se nombran los pines con su respectivo color
int LED_AMARILLO=A1;
int LED_VERDE=A2;
int i=0;//variable para el contador del led verde para intermitencia

void setup (){
  pinMode(LED_ROJO, OUTPUT);//se definen los led como pines de salida
  pinMode(LED_AMARILLO, OUTPUT);
  pinMode(LED_VERDE, OUTPUT);
 }
  
void loop(){
analogWrite(LED_ROJO,0);//se inicia con todos los led apagados para no alargar el codigo
analogWrite(LED_AMARILLO,0);
analogWrite(LED_VERDE,0);
delay(10);

analogWrite(LED_VERDE,676);//se utiliza 676 bits puesto que es el aproximado a 3.3 V en la conversión, donde 1023bits son 5V
delay(8000);//se enciende el led verde por 8 segundos

i=0;
while (i<5){
  analogWrite(LED_VERDE,0);//el led verde titila 4 veces con un tiempo de 0.3 segundos encendido y 0.3 apagado
  delay(300);
  analogWrite(LED_VERDE,676);
  delay(300);
  i=i+1;  
  }

analogWrite(LED_VERDE,0);//se apaga el led verde
analogWrite(LED_AMARILLO,676);//se enciende el led amarillo por 2.5 segundos
delay(2500);

analogWrite(LED_AMARILLO,0);//se apaga el led amarillo
analogWrite(LED_ROJO,676);//se enciende el led rojo por 7 segundos
delay(7000); 
}
